# Fritzing sketch Esquema_Projeto (saved by Fritzing 0.9.3b)
breadboards: 1

parts:
  Componente1 = Arduino Uno (Rev3)
  LCD1 = LCD screen
  R1 = Resistor [tolerance=±5% resistance=1k package=THT]
  C1 = Electrolytic Capacitor [capacitance=100µF voltage=16V package="100 mil [THT, electrolytic]"]
  C2 = Ceramic Capacitor [capacitance=100nF voltage=16V package="100 mil [THT, multilayer]"]
  U1 = mystery part, 4 pins [chip_label=DHT11]
  LED1 = LED - 5mm [color="Red (633nm)" package="5 mm [THT]"]
  LED2 = LED - 5mm [color="Red (633nm)" package="5 mm [THT]"]
  LED3 = LED - 5mm [color="Red (633nm)" package="5 mm [THT]"]
  LED4 = LED - 5mm [color="Red (633nm)" package="5 mm [THT]"]
  R2 = Resistor [tolerance=±5% resistance=1k package=THT]
  R3 = Resistor [tolerance=±5% resistance=1k package=THT]
  R4 = Resistor [tolerance=±5% resistance=1k package=THT]
  R5 = Resistor [tolerance=±5% resistance=1k package=THT]
  LED5 = LED - 5mm [color="Red (633nm)" package="5 mm [THT]"]
  R6 = Resistor [tolerance=±5% resistance=1k package=THT]

nets:
  N1: Componente1.A1, U1.pin2
  N2: Componente1.A2, R2.Pin_0
  N3: Componente1.A3, R3.Pin_0
  N4: Componente1.A4/SDA, R4.Pin_0
  N5: Componente1.A5/SCL, R5.Pin_0
  N6: Componente1.D9_PWM, R6.Pin_0
  GND: Componente1.GND, LCD1.VSS, LCD1.R/W, R1.Pin_0, C1.+, C2.1, U1.pin4, LED1.cathode, LED2.cathode, LED3.cathode, LED4.cathode
  N7: Componente1.D2, LCD1.RS
  N8: Componente1.D3_PWM, LCD1.E
  N9: Componente1.D4, LCD1.DB4
  N10: Componente1.D5_PWM, LCD1.DB5
  N11: Componente1.D6_PWM, LCD1.DB6
  N12: Componente1.D7, LCD1.DB7
  5V: Componente1.5V, LCD1.VDD, C1.-, C2.0, U1.pin1
  N13: LCD1.V0, R1.Pin_1
  N14: LED1.anode, R2.Pin_1
  N15: LED2.anode, R3.Pin_1
  N16: LED3.anode, R4.Pin_1
  N17: LED4.anode, R5.Pin_1
  N18: LED5.anode, R6.Pin_1
